// Logisim project Bcd_to_seven_segment.circ as structural Verilog: 1 circuit, main circuit main
module main (
  input  in_1,
  input  B,
  input  in_3,
  input  in_4,
  output a,
  output out_6,
  output c,
  output d,
  output e,
  output f,
  output g
);

  wire and_1_out, and_2_out, and_3_out, and_4_out, and_5_out, and_6_out, and_7_out, and_8_out, and_9_out,
       and_10_out, and_11_out, and_12_out, and_13_out, and_14_out, and_15_out, and_16_out, not_1_out,
       not_2_out, not_3_out;

  not not_1 (not_1_out, B);
  not not_2 (not_2_out, in_3);
  not not_3 (not_3_out, in_4);
  and and_1 (and_1_out, not_1_out, not_3_out);
  and and_2 (and_2_out, B, in_4);
  and and_3 (and_3_out, not_2_out, not_3_out);
  and and_4 (and_4_out, in_3, in_4);
  or or_1 (c, not_2_out, in_4, B);
  and and_5 (and_5_out, not_1_out, not_3_out);
  and and_6 (and_6_out, not_1_out, in_3);
  and and_7 (and_7_out, B, not_2_out, in_4);
  and and_8 (and_8_out, in_3, not_3_out);
  and and_9 (and_9_out, not_1_out, not_3_out);
  and and_10 (and_10_out, in_3, not_3_out);
  and and_11 (and_11_out, not_2_out, not_3_out);
  and and_12 (and_12_out, B, not_2_out);
  and and_13 (and_13_out, B, not_3_out);
  and and_14 (and_14_out, not_1_out, in_3);
  and and_15 (and_15_out, B, not_2_out);
  and and_16 (and_16_out, in_3, not_3_out);
  or or_2 (a, and_1_out, in_3, and_2_out, in_1);
  or or_3 (out_6, not_1_out, and_3_out, and_4_out);
  or or_4 (d, and_5_out, and_6_out, and_7_out, and_8_out, in_1);
  or or_5 (e, and_9_out, and_10_out);
  or or_6 (f, and_11_out, and_12_out, and_13_out, in_1);
  or or_7 (g, and_14_out, and_15_out, in_1, and_16_out);
  _7_Segment_Display u_7_segment_display_1 (.g(g), .f(f), .a(a), .b(out_6), .e(e), .d(d), .c(c));  // open: dp
endmodule
